# Fritzing sketch AQ_Board (saved by Fritzing 0.8.7b)
circuit board: 5.10396cm x 3.8654cm
breadboards: 1

parts:
  4_7k_Ohm = Resistor [tolerance=±5% resistance=220 package=THT]
  DS18B20_1 = female pin header, 3 pins [form="♀ (female)"]
  DS18B20_2 = female pin header, 3 pins [form="♀ (female)"]
  part = female pin header, 3 pins [form="♀ (female)"]

nets:
  N1: 4_7k_Ohm.Pin_0, DS18B20_1.pin2, DS18B20_2.pin2, part.pin2
  N2: 4_7k_Ohm.Pin_1, DS18B20_1.pin1, DS18B20_2.pin1, part.pin3
  N3: DS18B20_1.pin3, DS18B20_2.pin3, part.pin1
